# Fritzing sketch lab3Fritzing (saved by Fritzing 0.9.4)
breadboards: 1

parts:
  Part1 = Arduino Uno (Rev3)
  LED1 = RGB LED (com. cathode, rgb) [package="5 mm [THT]"]
  R1 = Resistor [tolerance=±5% resistance=220 package=THT]
  R2 = Resistor [tolerance=±5% resistance=220 package=THT]
  R3 = Resistor [tolerance=±5% resistance=220 package=THT]
  R4 = Rotary Potentiometer (Small) [maximum_resistance=100kΩ package=THT]

nets:
  N1: Part1.A0, R4.wiper
  N2: Part1.D8, R2.Pin_1
  N3: Part1.D9_PWM, R1.Pin_1
  N4: Part1.GND, LED1.common_cathode, R4.leg1
  N5: Part1.D7, R3.Pin_1
  N6: Part1.5V, R4.leg2
  N7: LED1.red_anode, R1.Pin_0
  N8: LED1.green_anode, R2.Pin_0
  N9: LED1.blue_anode, R3.Pin_0
